# Fritzing sketch Simple_OLED_GPS (saved by Fritzing 0.9.4)
circuit board: 8.46667cm x 5.64444cm
breadboards: 1

parts:
  Composant1 = Arduino Nano (Rev3.0)
  OLED1 = OLED 128x64 I2C Monochrome Display
  Composant2 = u-blox NEO-6M GPS Breakout

nets:
  GND: Composant1.GND, OLED1.GND, Composant2.GND
  N1: Composant1.D2, Composant2.TXD
  N2: Composant1.D3, Composant2.RXD
  5V: Composant1.5V, OLED1.VDD, Composant2.VCC
  N3: Composant1.A5, OLED1.SCK
  N4: Composant1.A4, OLED1.SDA
